// Logisim project Basico.circ as structural Verilog: 2 circuits, main circuit main
module main (
  input  in_1,
  input  in_2,
  input  in_3,
  input  in_4,
  input  in_5,
  input  in_6,
  input  in_7,
  output out_8,
  output out_9,
  output out_10,
  output out_11
);

  wire button_1_out;

  Button button_1 (.out(button_1_out));
  LED led_1 (.in(button_1_out));
  not not_1 (out_9, in_2);
  and and_1 (out_11, in_5, in_7);
  or or_1 (out_8, in_1, in_3);
  xor xor_1 (out_10, in_4, in_6);
endmodule

module PortaAND (
  input  A,
  input  B,
  output Saida
);

  wire transistor_1_out;

  Transistor #(.\type ("n")) transistor_1 (.in(1'b1), .out(transistor_1_out), .gate(A));
  Transistor #(.\type ("n")) transistor_2 (.in(transistor_1_out), .out(Saida), .gate(B));
  Pull_Resistor pull_resistor_1 (.node(Saida));
endmodule
