// Logisim project PortasLogicas.circ as structural Verilog: 9 circuits, main circuit Teste  das Portas Lógcas
module \Teste__das_Portas_Lógcas  (
  input  Entrada_A,
  input  Entrada_B,
  output out_3,
  output out_4,
  output out_5,
  output out_6,
  output out_7,
  output out_8,
  output out_9,
  output out_10
);

  // Probe on Entrada_A
  // Probe on Entrada_B
  PortaAND portaand_1 (.A(Entrada_A), .B(Entrada_B), .Saida(out_3));
  PortaOR portaor_1 (.A(Entrada_A), .B(Entrada_B), .Saida(out_4));
  PortaNOT portanot_1 (.Entrada(Entrada_A), .Saida(out_5));
  PortaBuffer portabuffer_1 (.Entrada(Entrada_A), .Saida(out_6));
  PortaNAND portanand_1 (.A(Entrada_A), .B(Entrada_B), .\Saída (out_7));
  PortaNOR portanor_1 (.A(Entrada_A), .B(Entrada_B), .\Saída (out_8));
  PortaXOR portaxor_1 (.A(Entrada_A), .B(Entrada_B), .\Saída (out_9));
  PortaXNOR portaxnor_1 (.A(Entrada_A), .B(Entrada_B), .\Saída (out_10));

  // Notes on the sheet:
  //   Estas portas já exstem prontas no LogSim
  //   mas aqui são "refeitas" para fins didáticos
endmodule

module PortaAND (
  input  A,
  input  B,
  output Saida
);

  wire transistor_1_out;

  Transistor #(.\type ("n")) transistor_1 (.in(1'b1), .out(transistor_1_out), .gate(A));
  Transistor #(.\type ("n")) transistor_2 (.in(transistor_1_out), .out(Saida), .gate(B));
  Pull_Resistor pull_resistor_1 (.node(Saida));

  // Notes on the sheet:
  //   Porta AND utilizando transístores
endmodule

module PortaOR (
  input  A,
  input  B,
  output Saida
);

  Transistor #(.\type ("n")) transistor_1 (.in(1'b1), .out(Saida), .gate(A));
  Pull_Resistor pull_resistor_1 (.node(Saida));
  Transistor #(.\type ("n")) transistor_2 (.in(1'b1), .out(Saida), .gate(B));

  // Notes on the sheet:
  //   Porta OR utilizando transístores
endmodule

module PortaNOT (
  input  Entrada,
  output Saida
);

  Transistor transistor_1 (.in(1'b1), .out(Saida), .gate(Entrada));
  Pull_Resistor pull_resistor_1 (.node(Saida));

  // Notes on the sheet:
  //   Porta NOT utilizando transístor tipo P
endmodule

module PortaBuffer (
  input  Entrada,
  output Saida
);

  Transistor #(.\type ("n")) transistor_1 (.in(1'b1), .out(Saida), .gate(Entrada));
  Pull_Resistor pull_resistor_1 (.node(Saida));

  // Notes on the sheet:
  //   BUFFER utilizando transístor tipo N
endmodule

module PortaNAND (
  input  A,
  input  B,
  output \Saída 
);

  wire portaand_1_saida;

  PortaAND portaand_1 (.A(A), .B(B), .Saida(portaand_1_saida));
  PortaNOT portanot_1 (.Entrada(portaand_1_saida), .Saida(\Saída ));
endmodule

module PortaNOR (
  input  A,
  input  B,
  output \Saída 
);

  wire portaor_1_saida;

  PortaOR portaor_1 (.A(A), .B(B), .Saida(portaor_1_saida));
  PortaNOT portanot_1 (.Entrada(portaor_1_saida), .Saida(\Saída ));
endmodule

module PortaXOR (
  input  A,
  input  B,
  output \Saída 
);

  wire portaand_1_saida, portanot_1_saida, portaor_1_saida;

  PortaOR portaor_1 (.A(A), .B(B), .Saida(portaor_1_saida));
  PortaAND portaand_1 (.A(A), .B(B), .Saida(portaand_1_saida));
  PortaNOT portanot_1 (.Entrada(portaand_1_saida), .Saida(portanot_1_saida));
  PortaAND portaand_2 (.A(portaor_1_saida), .B(portanot_1_saida), .Saida(\Saída ));
endmodule

module PortaXNOR (
  input  A,
  input  B,
  output \Saída 
);

  wire \portaxor_1_saída ;

  PortaXOR portaxor_1 (.A(A), .B(B), .\Saída (\portaxor_1_saída ));
  PortaNOT portanot_1 (.Entrada(\portaxor_1_saída ), .Saida(\Saída ));
endmodule
