// Logisim project Registradores.circ as structural Verilog: 6 circuits, main circuit Teste dos Registradores
module Teste_dos_Registradores (
  input  [15:0] Dado_a_ser_armazenado,
  output [11:0] _12bits_armazenados,
  output _1bit_armazenado,
  output [3:0] _4bits_armazenados,
  output [7:0] _8bits_armazenados,
  output [15:0] _16bits_armazenados
);

  wire clock_1_out, R, W;

  Button Armazenar (.out(W));
  Button Ler_dados_armazenados (.out(R));
  Registrador12bits registrador12bits_1 (
    .Dado_Entrada_bit_0(Dado_a_ser_armazenado[0]), .Dado_Entrada_bit_1(Dado_a_ser_armazenado[1]),
    .Dado_Entrada_bit_2(Dado_a_ser_armazenado[2]), .Dado_Entrada_bit_3(Dado_a_ser_armazenado[3]),
    .Dado_Entrada_bit_4(Dado_a_ser_armazenado[4]), .Dado_Entrada_bit_5(Dado_a_ser_armazenado[5]),
    .Dado_Entrada_bit_6(Dado_a_ser_armazenado[6]), .Dado_Entrada_bit_7(Dado_a_ser_armazenado[7]),
    .Dado_Entrada_bit_8(Dado_a_ser_armazenado[8]), .Dado_Entrada_bit_9(Dado_a_ser_armazenado[9]),
    .Dado_Entrada_bit_10(Dado_a_ser_armazenado[10]), .Dado_Entrada_bit_11(Dado_a_ser_armazenado[11]),
    .Gravar(W), .Clock(clock_1_out), .Dado_Armazenado_bit_0(_12bits_armazenados[0]),
    .Dado_Armazenado_bit_1(_12bits_armazenados[1]), .Dado_Armazenado_bit_2(_12bits_armazenados[2]),
    .Dado_Armazenado_bit_3(_12bits_armazenados[3]), .Dado_Armazenado_bit_4(_12bits_armazenados[4]),
    .Dado_Armazenado_bit_5(_12bits_armazenados[5]), .Dado_Armazenado_bit_6(_12bits_armazenados[6]),
    .Dado_Armazenado_bit_7(_12bits_armazenados[7]), .Dado_Armazenado_bit_8(_12bits_armazenados[8]),
    .Dado_Armazenado_bit_9(_12bits_armazenados[9]), .Dado_Armazenado_bit_10(_12bits_armazenados[10]),
    .Dado_Armazenado_bit_11(_12bits_armazenados[11]), .Ler(R));
  Registrador16bits registrador16bits_1 (
    .Dado_Entrada_bit_0(Dado_a_ser_armazenado[0]), .Dado_Entrada_bit_1(Dado_a_ser_armazenado[1]),
    .Dado_Entrada_bit_2(Dado_a_ser_armazenado[2]), .Dado_Entrada_bit_3(Dado_a_ser_armazenado[3]),
    .Dado_Entrada_bit_4(Dado_a_ser_armazenado[4]), .Dado_Entrada_bit_5(Dado_a_ser_armazenado[5]),
    .Dado_Entrada_bit_6(Dado_a_ser_armazenado[6]), .Dado_Entrada_bit_7(Dado_a_ser_armazenado[7]),
    .Dado_Entrada_bit_8(Dado_a_ser_armazenado[8]), .Dado_Entrada_bit_9(Dado_a_ser_armazenado[9]),
    .Dado_Entrada_bit_10(Dado_a_ser_armazenado[10]), .Dado_Entrada_bit_11(Dado_a_ser_armazenado[11]),
    .Dado_Entrada_bit_12(Dado_a_ser_armazenado[12]), .Dado_Entrada_bit_13(Dado_a_ser_armazenado[13]),
    .Dado_Entrada_bit_14(Dado_a_ser_armazenado[14]), .Dado_Entrada_bit_15(Dado_a_ser_armazenado[15]),
    .Gravar(W), .Clock(clock_1_out), .Dado_Armazenado_bit_0(_16bits_armazenados[0]),
    .Dado_Armazenado_bit_1(_16bits_armazenados[1]), .Dado_Armazenado_bit_2(_16bits_armazenados[2]),
    .Dado_Armazenado_bit_3(_16bits_armazenados[3]), .Dado_Armazenado_bit_4(_16bits_armazenados[4]),
    .Dado_Armazenado_bit_5(_16bits_armazenados[5]), .Dado_Armazenado_bit_6(_16bits_armazenados[6]),
    .Dado_Armazenado_bit_7(_16bits_armazenados[7]), .Dado_Armazenado_bit_8(_16bits_armazenados[8]),
    .Dado_Armazenado_bit_9(_16bits_armazenados[9]), .Dado_Armazenado_bit_10(_16bits_armazenados[10]),
    .Dado_Armazenado_bit_11(_16bits_armazenados[11]), .Dado_Armazenado_bit_12(_16bits_armazenados[12]),
    .Dado_Armazenado_bit_13(_16bits_armazenados[13]), .Dado_Armazenado_bit_14(_16bits_armazenados[14]),
    .Dado_Armazenado_bit_15(_16bits_armazenados[15]), .Ler(R));
  Clock clock_1 (.out(clock_1_out));
  Registrador1bit registrador1bit_1 (
    .Dado_Entrada(Dado_a_ser_armazenado[0]), .Gravar(W), .Clock(clock_1_out),
    .Dado_Armazenado(_1bit_armazenado), .Ler(R));
  Registrador4bits registrador4bits_1 (
    .Dado_Entrada_bit_0(Dado_a_ser_armazenado[0]), .Dado_Entrada_bit_1(Dado_a_ser_armazenado[1]),
    .Dado_Entrada_bit_2(Dado_a_ser_armazenado[2]), .Dado_Entrada_bit_3(Dado_a_ser_armazenado[3]), .Gravar(W),
    .Clock(clock_1_out), .Dado_Armazenado_bit_0(_4bits_armazenados[0]),
    .Dado_Armazenado_bit_1(_4bits_armazenados[1]), .Dado_Armazenado_bit_2(_4bits_armazenados[2]),
    .Dado_Armazenado_bit_3(_4bits_armazenados[3]), .Ler(R));
  Registrador8bits registrador8bits_1 (
    .Dado_Entrada_bit_0(Dado_a_ser_armazenado[0]), .Dado_Entrada_bit_1(Dado_a_ser_armazenado[1]),
    .Dado_Entrada_bit_2(Dado_a_ser_armazenado[2]), .Dado_Entrada_bit_3(Dado_a_ser_armazenado[3]),
    .Dado_Entrada_bit_4(Dado_a_ser_armazenado[4]), .Dado_Entrada_bit_5(Dado_a_ser_armazenado[5]),
    .Dado_Entrada_bit_6(Dado_a_ser_armazenado[6]), .Dado_Entrada_bit_7(Dado_a_ser_armazenado[7]), .Gravar(W),
    .Clock(clock_1_out), .Dado_Armazenado_bit_0(_8bits_armazenados[0]),
    .Dado_Armazenado_bit_1(_8bits_armazenados[1]), .Dado_Armazenado_bit_2(_8bits_armazenados[2]),
    .Dado_Armazenado_bit_3(_8bits_armazenados[3]), .Dado_Armazenado_bit_4(_8bits_armazenados[4]),
    .Dado_Armazenado_bit_5(_8bits_armazenados[5]), .Dado_Armazenado_bit_6(_8bits_armazenados[6]),
    .Dado_Armazenado_bit_7(_8bits_armazenados[7]), .Ler(R));
endmodule

module Registrador1bit (
  input  Dado_Entrada,
  input  Gravar,
  input  Ler,
  input  Clock,
  output Dado_Armazenado
);

  wire and_1_out, and_2_out, nand_1_out, nand_2_out, nand_3_out, nand_4_out, not_1_out;

  not not_1 (not_1_out, Dado_Entrada);
  and and_1 (and_1_out, Gravar, Clock);
  nand nand_1 (nand_1_out, Dado_Entrada, and_1_out);
  nand nand_2 (nand_2_out, not_1_out, and_1_out);
  nand nand_3 (nand_3_out, nand_1_out, nand_4_out);
  and and_2 (and_2_out, Clock, Ler);
  nand nand_4 (nand_4_out, nand_3_out, nand_2_out);
  assign Dado_Armazenado = and_2_out ? nand_3_out : 1'bz;  // Controlled_Buffer controlled_buffer_1
endmodule

module Registrador4bits (
  input  Dado_Entrada_bit_0,
  input  Dado_Entrada_bit_1,
  input  Dado_Entrada_bit_2,
  input  Dado_Entrada_bit_3,
  input  Gravar,
  input  Ler,
  input  Clock,
  output Dado_Armazenado_bit_0,
  output Dado_Armazenado_bit_1,
  output Dado_Armazenado_bit_2,
  output Dado_Armazenado_bit_3
);

  Registrador1bit registrador1bit_1 (
    .Dado_Entrada(Dado_Entrada_bit_0), .Gravar(Gravar), .Clock(Clock),
    .Dado_Armazenado(Dado_Armazenado_bit_0), .Ler(Ler));
  Registrador1bit registrador1bit_2 (
    .Dado_Entrada(Dado_Entrada_bit_1), .Gravar(Gravar), .Clock(Clock),
    .Dado_Armazenado(Dado_Armazenado_bit_1), .Ler(Ler));
  Registrador1bit registrador1bit_3 (
    .Dado_Entrada(Dado_Entrada_bit_2), .Gravar(Gravar), .Clock(Clock),
    .Dado_Armazenado(Dado_Armazenado_bit_2), .Ler(Ler));
  Registrador1bit registrador1bit_4 (
    .Dado_Entrada(Dado_Entrada_bit_3), .Gravar(Gravar), .Clock(Clock),
    .Dado_Armazenado(Dado_Armazenado_bit_3), .Ler(Ler));
endmodule

module Registrador8bits (
  input  Dado_Entrada_bit_0,
  input  Dado_Entrada_bit_1,
  input  Dado_Entrada_bit_2,
  input  Dado_Entrada_bit_3,
  input  Dado_Entrada_bit_4,
  input  Dado_Entrada_bit_5,
  input  Dado_Entrada_bit_6,
  input  Dado_Entrada_bit_7,
  input  Gravar,
  input  Ler,
  input  Clock,
  output Dado_Armazenado_bit_0,
  output Dado_Armazenado_bit_1,
  output Dado_Armazenado_bit_2,
  output Dado_Armazenado_bit_3,
  output Dado_Armazenado_bit_4,
  output Dado_Armazenado_bit_5,
  output Dado_Armazenado_bit_6,
  output Dado_Armazenado_bit_7
);

  Registrador4bits registrador4bits_1 (
    .Dado_Entrada_bit_0(Dado_Entrada_bit_0), .Dado_Entrada_bit_1(Dado_Entrada_bit_1),
    .Dado_Entrada_bit_2(Dado_Entrada_bit_2), .Dado_Entrada_bit_3(Dado_Entrada_bit_3), .Gravar(Gravar),
    .Clock(Clock), .Dado_Armazenado_bit_0(Dado_Armazenado_bit_0),
    .Dado_Armazenado_bit_1(Dado_Armazenado_bit_1), .Dado_Armazenado_bit_2(Dado_Armazenado_bit_2),
    .Dado_Armazenado_bit_3(Dado_Armazenado_bit_3), .Ler(Ler));
  Registrador4bits registrador4bits_2 (
    .Dado_Entrada_bit_0(Dado_Entrada_bit_4), .Dado_Entrada_bit_1(Dado_Entrada_bit_5),
    .Dado_Entrada_bit_2(Dado_Entrada_bit_6), .Dado_Entrada_bit_3(Dado_Entrada_bit_7), .Gravar(Gravar),
    .Clock(Clock), .Dado_Armazenado_bit_0(Dado_Armazenado_bit_4),
    .Dado_Armazenado_bit_1(Dado_Armazenado_bit_5), .Dado_Armazenado_bit_2(Dado_Armazenado_bit_6),
    .Dado_Armazenado_bit_3(Dado_Armazenado_bit_7), .Ler(Ler));
endmodule

module Registrador12bits (
  input  Dado_Entrada_bit_0,
  input  Dado_Entrada_bit_1,
  input  Dado_Entrada_bit_2,
  input  Dado_Entrada_bit_3,
  input  Dado_Entrada_bit_4,
  input  Dado_Entrada_bit_5,
  input  Dado_Entrada_bit_6,
  input  Dado_Entrada_bit_7,
  input  Dado_Entrada_bit_8,
  input  Dado_Entrada_bit_9,
  input  Dado_Entrada_bit_10,
  input  Dado_Entrada_bit_11,
  input  Gravar,
  input  Ler,
  input  Clock,
  output Dado_Armazenado_bit_0,
  output Dado_Armazenado_bit_1,
  output Dado_Armazenado_bit_2,
  output Dado_Armazenado_bit_3,
  output Dado_Armazenado_bit_4,
  output Dado_Armazenado_bit_5,
  output Dado_Armazenado_bit_6,
  output Dado_Armazenado_bit_7,
  output Dado_Armazenado_bit_8,
  output Dado_Armazenado_bit_9,
  output Dado_Armazenado_bit_10,
  output Dado_Armazenado_bit_11
);

  Registrador4bits registrador4bits_1 (
    .Dado_Entrada_bit_0(Dado_Entrada_bit_0), .Dado_Entrada_bit_1(Dado_Entrada_bit_1),
    .Dado_Entrada_bit_2(Dado_Entrada_bit_2), .Dado_Entrada_bit_3(Dado_Entrada_bit_3), .Gravar(Gravar),
    .Clock(Clock), .Dado_Armazenado_bit_0(Dado_Armazenado_bit_0),
    .Dado_Armazenado_bit_1(Dado_Armazenado_bit_1), .Dado_Armazenado_bit_2(Dado_Armazenado_bit_2),
    .Dado_Armazenado_bit_3(Dado_Armazenado_bit_3), .Ler(Ler));
  Registrador4bits registrador4bits_2 (
    .Dado_Entrada_bit_0(Dado_Entrada_bit_4), .Dado_Entrada_bit_1(Dado_Entrada_bit_5),
    .Dado_Entrada_bit_2(Dado_Entrada_bit_6), .Dado_Entrada_bit_3(Dado_Entrada_bit_7), .Gravar(Gravar),
    .Clock(Clock), .Dado_Armazenado_bit_0(Dado_Armazenado_bit_4),
    .Dado_Armazenado_bit_1(Dado_Armazenado_bit_5), .Dado_Armazenado_bit_2(Dado_Armazenado_bit_6),
    .Dado_Armazenado_bit_3(Dado_Armazenado_bit_7), .Ler(Ler));
  Registrador4bits registrador4bits_3 (
    .Dado_Entrada_bit_0(Dado_Entrada_bit_8), .Dado_Entrada_bit_1(Dado_Entrada_bit_8),
    .Dado_Entrada_bit_2(Dado_Entrada_bit_10), .Dado_Entrada_bit_3(Dado_Entrada_bit_11), .Gravar(Gravar),
    .Clock(Clock), .Dado_Armazenado_bit_0(Dado_Armazenado_bit_8),
    .Dado_Armazenado_bit_1(Dado_Armazenado_bit_9), .Dado_Armazenado_bit_2(Dado_Armazenado_bit_10),
    .Dado_Armazenado_bit_3(Dado_Armazenado_bit_11), .Ler(Ler));

  assign Dado_Entrada_bit_9 = Dado_Entrada_bit_8;
endmodule

module Registrador16bits (
  input  Dado_Entrada_bit_0,
  input  Dado_Entrada_bit_1,
  input  Dado_Entrada_bit_2,
  input  Dado_Entrada_bit_3,
  input  Dado_Entrada_bit_4,
  input  Dado_Entrada_bit_5,
  input  Dado_Entrada_bit_6,
  input  Dado_Entrada_bit_7,
  input  Dado_Entrada_bit_8,
  input  Dado_Entrada_bit_9,
  input  Dado_Entrada_bit_10,
  input  Dado_Entrada_bit_11,
  input  Dado_Entrada_bit_12,
  input  Dado_Entrada_bit_13,
  input  Dado_Entrada_bit_14,
  input  Dado_Entrada_bit_15,
  input  Gravar,
  input  Ler,
  input  Clock,
  output Dado_Armazenado_bit_0,
  output Dado_Armazenado_bit_1,
  output Dado_Armazenado_bit_2,
  output Dado_Armazenado_bit_3,
  output Dado_Armazenado_bit_4,
  output Dado_Armazenado_bit_5,
  output Dado_Armazenado_bit_6,
  output Dado_Armazenado_bit_7,
  output Dado_Armazenado_bit_8,
  output Dado_Armazenado_bit_9,
  output Dado_Armazenado_bit_10,
  output Dado_Armazenado_bit_11,
  output Dado_Armazenado_bit_12,
  output Dado_Armazenado_bit_13,
  output Dado_Armazenado_bit_14,
  output Dado_Armazenado_bit_15
);

  Registrador8bits registrador8bits_1 (
    .Dado_Entrada_bit_0(Dado_Entrada_bit_0), .Dado_Entrada_bit_1(Dado_Entrada_bit_1),
    .Dado_Entrada_bit_2(Dado_Entrada_bit_2), .Dado_Entrada_bit_3(Dado_Entrada_bit_3),
    .Dado_Entrada_bit_4(Dado_Entrada_bit_4), .Dado_Entrada_bit_5(Dado_Entrada_bit_5),
    .Dado_Entrada_bit_6(Dado_Entrada_bit_6), .Dado_Entrada_bit_7(Dado_Entrada_bit_7), .Gravar(Gravar),
    .Clock(Clock), .Dado_Armazenado_bit_0(Dado_Armazenado_bit_0),
    .Dado_Armazenado_bit_1(Dado_Armazenado_bit_1), .Dado_Armazenado_bit_2(Dado_Armazenado_bit_2),
    .Dado_Armazenado_bit_3(Dado_Armazenado_bit_3), .Dado_Armazenado_bit_4(Dado_Armazenado_bit_4),
    .Dado_Armazenado_bit_5(Dado_Armazenado_bit_5), .Dado_Armazenado_bit_6(Dado_Armazenado_bit_6),
    .Dado_Armazenado_bit_7(Dado_Armazenado_bit_7), .Ler(Ler));
  Registrador8bits registrador8bits_2 (
    .Dado_Entrada_bit_0(Dado_Entrada_bit_8), .Dado_Entrada_bit_1(Dado_Entrada_bit_9),
    .Dado_Entrada_bit_2(Dado_Entrada_bit_10), .Dado_Entrada_bit_3(Dado_Entrada_bit_11),
    .Dado_Entrada_bit_4(Dado_Entrada_bit_12), .Dado_Entrada_bit_5(Dado_Entrada_bit_13),
    .Dado_Entrada_bit_6(Dado_Entrada_bit_14), .Dado_Entrada_bit_7(Dado_Entrada_bit_15), .Gravar(Gravar),
    .Clock(Clock), .Dado_Armazenado_bit_0(Dado_Armazenado_bit_8),
    .Dado_Armazenado_bit_1(Dado_Armazenado_bit_9), .Dado_Armazenado_bit_2(Dado_Armazenado_bit_10),
    .Dado_Armazenado_bit_3(Dado_Armazenado_bit_11), .Dado_Armazenado_bit_4(Dado_Armazenado_bit_12),
    .Dado_Armazenado_bit_5(Dado_Armazenado_bit_13), .Dado_Armazenado_bit_6(Dado_Armazenado_bit_14),
    .Dado_Armazenado_bit_7(Dado_Armazenado_bit_15), .Ler(Ler));
endmodule
