// Logisim project Registradores_e_RAM.circ as structural Verilog: 4 circuits, main circuit main
module main (
  input  Gravar,
  input  [7:0] Dado_de_entrada,
  input  [2:0] \Endereço ,
  output [7:0] \Dado_de_saída 
);

  wire clock_1_out, not_1_out;

  Clock clock_1 (.out(clock_1_out));
  RAM #(.addrWidth(3)) ram_1 (
    .addr(\Endereço ), .data(\Dado_de_saída ), .sel(1'b1), .clk(clock_1_out), .ld(not_1_out));  // open: clr
  not not_1 (not_1_out, Gravar);
  assign \Dado_de_saída  = Gravar ? Dado_de_entrada : 8'bz;  // Controlled_Buffer controlled_buffer_1
endmodule

module AndOrLatch (
  input  in_1,
  input  in_2,
  output out_3
);

  wire not_1_out, or_1_out;

  or or_1 (or_1_out, out_3, in_1);
  not not_1 (not_1_out, in_2);
  and and_1 (out_3, or_1_out, not_1_out);

  // Notes on the sheet:
  //   AND / OR Latch
endmodule

module GatedLatch (
  input  Dado_entrando,
  input  \Habilita_gravação ,
  output Dado_armazenado
);

  wire and_1_out, and_2_out, and_3_out, clock_1_out, not_1_out, not_2_out, or_1_out;

  and and_1 (and_1_out, \Habilita_gravação , clock_1_out);
  not not_1 (not_1_out, Dado_entrando);
  Clock clock_1 (.out(clock_1_out));
  and and_2 (and_2_out, Dado_entrando, and_1_out);
  and and_3 (and_3_out, not_1_out, and_1_out);
  or or_1 (or_1_out, Dado_armazenado, and_2_out);
  not not_2 (not_2_out, and_3_out);
  and and_4 (Dado_armazenado, or_1_out, not_2_out);
endmodule

module Registrador8bits (
  input  in_1,
  input  in_2,
  input  in_3,
  input  in_4,
  input  in_5,
  input  in_6,
  input  in_7,
  input  in_8,
  input  \Habilita_gravação ,
  output out_10,
  output out_11,
  output out_12,
  output out_13,
  output out_14,
  output out_15,
  output out_16,
  output out_17
);

  GatedLatch gatedlatch_1 (.Dado_entrando(in_1), .\Habilita_gravação (\Habilita_gravação ), .Dado_armazenado(out_10));
  GatedLatch gatedlatch_2 (.Dado_entrando(in_2), .\Habilita_gravação (\Habilita_gravação ), .Dado_armazenado(out_11));
  GatedLatch gatedlatch_3 (.Dado_entrando(in_3), .\Habilita_gravação (\Habilita_gravação ), .Dado_armazenado(out_12));
  GatedLatch gatedlatch_4 (.Dado_entrando(in_4), .\Habilita_gravação (\Habilita_gravação ), .Dado_armazenado(out_13));
  GatedLatch gatedlatch_5 (.Dado_entrando(in_5), .\Habilita_gravação (\Habilita_gravação ), .Dado_armazenado(out_14));
  GatedLatch gatedlatch_6 (.Dado_entrando(in_6), .\Habilita_gravação (\Habilita_gravação ), .Dado_armazenado(out_15));
  GatedLatch gatedlatch_7 (.Dado_entrando(in_7), .\Habilita_gravação (\Habilita_gravação ), .Dado_armazenado(out_16));
  GatedLatch gatedlatch_8 (.Dado_entrando(in_8), .\Habilita_gravação (\Habilita_gravação ), .Dado_armazenado(out_17));
endmodule
