// Logisim project Somador_e_ULA.circ as structural Verilog: 5 circuits, main circuit main
module main (
  input  in_1,
  input  in_2,
  input  in_3,
  input  in_4,
  input  in_5,
  input  in_6,
  input  in_7,
  input  in_8,
  input  in_9,
  input  in_10,
  input  in_11,
  input  in_12,
  input  in_13,
  input  in_14,
  input  in_15,
  input  in_16,
  output out_17,
  output out_18,
  output out_19,
  output out_20,
  output out_21,
  output out_22,
  output out_23,
  output out_24,
  output out_25,
  output out_26,
  output out_27
);

  wire undriven;

  Comparator comparator_1 (
    .a({in_9, in_10, in_11, in_12, in_13, in_14, in_15, in_16}),
    .b({in_1, in_2, in_3, in_4, in_5, in_6, in_7, in_8}), .gt(out_25), .eq(out_26), .lt(out_27));
  ULA ula_1 (
    .A2(undriven), .A1(undriven), .A0(undriven), .B7(undriven));  // open: Soma, Subtração, Lógica, Overflow, Zero, Negativo, Igual, Maior, Menor, A7, A6, A5, A4, A3, B6, B5, B4, B3, B2, B1, B0, S7, S6, S5, S4, S3, S2, S1, S0
endmodule

module SomadorSimples (
  input  A,
  input  B,
  output S,
  output C
);

  xor xor_1 (S, A, B);
  and and_1 (C, A, B);

  // Notes on the sheet:
  //   Half Adder
endmodule

module SomadorCompleto (
  input  C_in,
  input  A,
  input  B,
  output S,
  output C_out
);

  wire somadorsimples_1_c, somadorsimples_1_s, somadorsimples_2_c;

  SomadorSimples somadorsimples_1 (.A(A), .B(B), .S(somadorsimples_1_s), .C(somadorsimples_1_c));
  SomadorSimples somadorsimples_2 (.A(somadorsimples_1_s), .B(C_in), .S(S), .C(somadorsimples_2_c));
  or or_1 (C_out, somadorsimples_1_c, somadorsimples_2_c);
endmodule

module Somador8bits (
  input  in_1,
  input  in_2,
  input  in_3,
  input  in_4,
  input  in_5,
  input  in_6,
  input  in_7,
  input  in_8,
  input  in_9,
  input  in_10,
  input  in_11,
  input  in_12,
  input  in_13,
  input  in_14,
  input  in_15,
  input  in_16,
  output out_17,
  output out_18,
  output out_19,
  output out_20,
  output out_21,
  output out_22,
  output out_23,
  output out_24,
  output out_25
);

  wire somadorcompleto_1_c_out, somadorcompleto_2_c_out, somadorcompleto_3_c_out, somadorcompleto_4_c_out,
       somadorcompleto_5_c_out, somadorcompleto_6_c_out, somadorsimples_1_c;

  SomadorSimples somadorsimples_1 (.A(in_16), .B(in_8), .S(out_24), .C(somadorsimples_1_c));
  SomadorCompleto somadorcompleto_1 (
    .A(in_15), .B(in_7), .C_in(somadorsimples_1_c), .C_out(somadorcompleto_1_c_out), .S(out_23));
  SomadorCompleto somadorcompleto_2 (
    .A(in_14), .B(in_6), .C_in(somadorcompleto_1_c_out), .C_out(somadorcompleto_2_c_out), .S(out_22));
  SomadorCompleto somadorcompleto_3 (
    .A(in_13), .B(in_5), .C_in(somadorcompleto_2_c_out), .C_out(somadorcompleto_3_c_out), .S(out_21));
  SomadorCompleto somadorcompleto_4 (
    .A(in_12), .B(in_4), .C_in(somadorcompleto_3_c_out), .C_out(somadorcompleto_4_c_out), .S(out_20));
  SomadorCompleto somadorcompleto_5 (
    .A(in_11), .B(in_3), .C_in(somadorcompleto_4_c_out), .C_out(somadorcompleto_5_c_out), .S(out_19));
  SomadorCompleto somadorcompleto_6 (
    .A(in_10), .B(in_2), .C_in(somadorcompleto_5_c_out), .C_out(somadorcompleto_6_c_out), .S(out_18));
  SomadorCompleto somadorcompleto_7 (.A(in_9), .B(in_1), .C_in(somadorcompleto_6_c_out), .C_out(out_25), .S(out_17));
endmodule

module ULA (
  input  A7,
  input  A6,
  input  A5,
  input  A4,
  input  A3,
  input  A2,
  input  A1,
  input  A0,
  input  B7,
  input  B6,
  input  B5,
  input  B4,
  input  B3,
  input  B2,
  input  B1,
  input  B0,
  input  Soma,
  input  \Subtração ,
  input  \Lógica ,
  output Overflow,
  output Zero,
  output Negativo,
  output Igual,
  output Maior,
  output Menor,
  output S7,
  output S6,
  output S5,
  output S4,
  output S3,
  output S2,
  output S1,
  output S0
);

  wire adder_1_cout, comparator_1_eq, comparator_1_gt, comparator_1_lt;
  wire [7:0] adder_1_out, subtractor_1_out;

  Adder adder_1 (
    .a({A7, A6, A5, A4, A3, A2, A1, A0}), .b({B7, B6, B5, B4, B3, B2, B1, B0}), .out(adder_1_out),
    .cout(adder_1_cout));  // open: cin
  Subtractor subtractor_1 (
    .a({A7, A6, A5, A4, A3, A2, A1, A0}), .b({B7, B6, B5, B4, B3, B2, B1, B0}), .out(subtractor_1_out));  // open: bin, bout
  Comparator comparator_1 (
    .a({A7, A6, A5, A4, A3, A2, A1, A0}), .b({B7, B6, B5, B4, B3, B2, B1, B0}), .gt(comparator_1_gt),
    .eq(comparator_1_eq), .lt(comparator_1_lt));
  Comparator comparator_2 (.a({S7, S6, S5, S4, S3, S2, S1, S0}), .b({8{1'b0}}), .eq(Zero), .lt(Negativo));  // open: gt
  assign {S7, S6, S5, S4, S3, S2, S1, S0} = Soma ? adder_1_out : 8'bz;  // Controlled_Buffer controlled_buffer_1
  assign Overflow = Soma ? adder_1_cout : 1'bz;  // Controlled_Buffer controlled_buffer_2
  assign {S7, S6, S5, S4, S3, S2, S1, S0} = \Subtração  ? subtractor_1_out : 8'bz;  // Controlled_Buffer controlled_buffer_3
  assign Maior = \Lógica  ? comparator_1_gt : 1'bz;  // Controlled_Buffer controlled_buffer_4
  assign Igual = \Lógica  ? comparator_1_eq : 1'bz;  // Controlled_Buffer controlled_buffer_5
  assign Menor = \Lógica  ? comparator_1_lt : 1'bz;  // Controlled_Buffer controlled_buffer_6
endmodule
