// Logisim project Somadores.circ as structural Verilog: 6 circuits, main circuit Teste dos Somadores
module Teste_dos_Somadores (
  input  A,
  input  [15:0] \Número_A ,
  input  [15:0] \Número_B ,
  input  B,
  input  A_2,
  input  B_2
);

  wire meiosomador_1_e, meiosomador_1_s, somadorcompleto_1_cout, somadorcompleto_1_s;
  wire [3:0] somador4bits_1_s0;
  wire [7:0] somador8bits_1_s0;
  wire [15:0] somador16bits_1_s0;

  // Probe on \Número_A 
  Somador4bits somador4bits_1 (
    .Cin(1'b0), .A3(\Número_A [3]), .A2(\Número_A [2]), .A1(\Número_A [1]), .A0(\Número_A [0]),
    .B3(\Número_B [3]), .B2(\Número_B [2]), .B1(\Número_B [1]), .B0(\Número_B [0]),
    .S3(somador4bits_1_s0[3]), .S2(somador4bits_1_s0[2]), .S1(somador4bits_1_s0[1]), .S0(somador4bits_1_s0[0]));  // open: Cout
  // Probe on somador4bits_1_s0
  // Probe on \Número_B 
  // Probe on somador16bits_1_s0
  Somador16bits somador16bits_1 (
    .A15(\Número_A [15]), .A14(\Número_A [14]), .A13(\Número_A [13]), .A12(\Número_A [12]),
    .A11(\Número_A [11]), .A10(\Número_A [10]), .A9(\Número_A [9]), .A8(\Número_A [8]), .A7(\Número_A [7]),
    .A6(\Número_A [6]), .A5(\Número_A [5]), .A4(\Número_A [4]), .A3(\Número_A [3]), .A2(\Número_A [2]),
    .A1(\Número_A [1]), .A0(\Número_A [0]), .B15(\Número_B [15]), .B14(\Número_B [14]), .B13(\Número_B [13]),
    .B12(\Número_B [12]), .B11(\Número_B [11]), .B10(\Número_B [10]), .B9(\Número_B [9]), .B8(\Número_B [8]),
    .B7(\Número_B [7]), .B6(\Número_B [6]), .B5(\Número_B [5]), .B4(\Número_B [4]), .B3(\Número_B [3]),
    .B2(\Número_B [2]), .B1(\Número_B [1]), .B0(\Número_B [0]), .S15(somador16bits_1_s0[15]),
    .S14(somador16bits_1_s0[14]), .S13(somador16bits_1_s0[13]), .S12(somador16bits_1_s0[12]),
    .S11(somador16bits_1_s0[11]), .S10(somador16bits_1_s0[10]), .S9(somador16bits_1_s0[9]),
    .S8(somador16bits_1_s0[8]), .S7(somador16bits_1_s0[7]), .S6(somador16bits_1_s0[6]),
    .S5(somador16bits_1_s0[5]), .S4(somador16bits_1_s0[4]), .S3(somador16bits_1_s0[3]),
    .S2(somador16bits_1_s0[2]), .S1(somador16bits_1_s0[1]), .S0(somador16bits_1_s0[0]), .Cin(1'b0));  // open: Cout
  MeioSomador meiosomador_1 (.A(A), .B(B), .S(meiosomador_1_s), .E(meiosomador_1_e));
  SomadorCompleto somadorcompleto_1 (
    .Cin(meiosomador_1_e), .A(A_2), .B(B_2), .S(somadorcompleto_1_s), .Cout(somadorcompleto_1_cout));
  Somador8bits somador8bits_1 (
    .Cin(1'b0), .A7(\Número_A [7]), .A6(\Número_A [6]), .A5(\Número_A [5]), .A4(\Número_A [4]),
    .A3(\Número_A [3]), .A2(\Número_A [2]), .A1(\Número_A [1]), .A0(\Número_A [0]), .B7(\Número_B [7]),
    .B6(\Número_B [6]), .B5(\Número_B [5]), .B4(\Número_B [4]), .B3(\Número_B [3]), .B2(\Número_B [2]),
    .B1(\Número_B [1]), .B0(\Número_B [0]), .S7(somador8bits_1_s0[7]), .S6(somador8bits_1_s0[6]),
    .S5(somador8bits_1_s0[5]), .S4(somador8bits_1_s0[4]), .S3(somador8bits_1_s0[3]),
    .S2(somador8bits_1_s0[2]), .S1(somador8bits_1_s0[1]), .S0(somador8bits_1_s0[0]));  // open: Cout
  // Probe on somador8bits_1_s0
  // Probe on A
  // Probe on B
  // Probe on meiosomador_1_e
  // Probe on meiosomador_1_s
  // Probe on meiosomador_1_e
  // Probe on A_2
  // Probe on B_2
  // Probe on somadorcompleto_1_cout
  // Probe on somadorcompleto_1_s

  // Notes on the sheet:
  //   +
  //   _____
  //   +
  //   +
  //   _____
endmodule

module MeioSomador (
  input  A,
  input  B,
  output S,
  output E
);

  xor xor_1 (S, A, B);
  and and_1 (E, B, A);
endmodule

module SomadorCompleto (
  input  Cin,
  input  A,
  input  B,
  output S,
  output Cout
);

  wire meiosomador_1_e, meiosomador_1_s, meiosomador_2_e;

  MeioSomador meiosomador_1 (.A(A), .B(B), .S(meiosomador_1_s), .E(meiosomador_1_e));
  MeioSomador meiosomador_2 (.A(Cin), .B(meiosomador_1_s), .S(S), .E(meiosomador_2_e));
  or or_1 (Cout, meiosomador_2_e, meiosomador_1_e);
endmodule

module Somador4bits (
  input  Cin,
  input  A3,
  input  A2,
  input  A1,
  input  A0,
  input  B3,
  input  B2,
  input  B1,
  input  B0,
  output S3,
  output S2,
  output S1,
  output S0,
  output Cout
);

  wire somadorcompleto_2_cout, somadorcompleto_3_cout, somadorcompleto_4_cout;

  SomadorCompleto somadorcompleto_1 (.Cin(somadorcompleto_2_cout), .A(B3), .B(A3), .S(S3), .Cout(Cout));
  SomadorCompleto somadorcompleto_2 (
    .Cin(somadorcompleto_3_cout), .A(B2), .B(A2), .S(S2), .Cout(somadorcompleto_2_cout));
  SomadorCompleto somadorcompleto_3 (
    .Cin(somadorcompleto_4_cout), .A(B1), .B(A1), .S(S1), .Cout(somadorcompleto_3_cout));
  SomadorCompleto somadorcompleto_4 (.Cin(Cin), .A(B0), .B(A0), .S(S0), .Cout(somadorcompleto_4_cout));
endmodule

module Somador8bits (
  input  Cin,
  input  A7,
  input  A6,
  input  A5,
  input  A4,
  input  A3,
  input  A2,
  input  A1,
  input  A0,
  input  B7,
  input  B6,
  input  B5,
  input  B4,
  input  B3,
  input  B2,
  input  B1,
  input  B0,
  output S7,
  output S6,
  output S5,
  output S4,
  output S3,
  output S2,
  output S1,
  output S0,
  output Cout
);

  wire somador4bits_2_cout;

  Somador4bits somador4bits_1 (
    .Cout(Cout), .Cin(somador4bits_2_cout), .A3(A7), .A2(A6), .A1(A5), .A0(A4), .B3(B7), .B2(B6), .B1(B5),
    .B0(B4), .S3(S7), .S2(S6), .S1(S5), .S0(S4));
  Somador4bits somador4bits_2 (
    .Cout(somador4bits_2_cout), .Cin(Cin), .A3(A3), .A2(A2), .A1(A1), .A0(A0), .B3(B3), .B2(B2), .B1(B1),
    .B0(B0), .S3(S3), .S2(S2), .S1(S1), .S0(S0));
endmodule

module Somador16bits (
  input  Cin,
  input  A15,
  input  A14,
  input  A13,
  input  A12,
  input  A11,
  input  A10,
  input  A9,
  input  A8,
  input  A7,
  input  A6,
  input  A5,
  input  A4,
  input  A3,
  input  A2,
  input  A1,
  input  A0,
  input  B15,
  input  B14,
  input  B13,
  input  B12,
  input  B11,
  input  B10,
  input  B9,
  input  B8,
  input  B7,
  input  B6,
  input  B5,
  input  B4,
  input  B3,
  input  B2,
  input  B1,
  input  B0,
  output S15,
  output S14,
  output S13,
  output S12,
  output S11,
  output S10,
  output S9,
  output S8,
  output S7,
  output S6,
  output S5,
  output S4,
  output S3,
  output S2,
  output S1,
  output S0,
  output Cout
);

  wire somador8bits_2_cout;

  Somador8bits somador8bits_1 (
    .Cout(Cout), .Cin(somador8bits_2_cout), .A7(A15), .A6(A14), .A5(A13), .A4(A12), .A3(A11), .A2(A10),
    .A1(A9), .A0(A8), .B7(B15), .B6(B14), .B5(B13), .B4(B12), .B3(B11), .B2(B10), .B1(B9), .B0(B8), .S7(S15),
    .S6(S14), .S5(S13), .S4(S12), .S3(S11), .S2(S10), .S1(S9), .S0(S8));
  Somador8bits somador8bits_2 (
    .Cout(somador8bits_2_cout), .Cin(Cin), .A7(A7), .A6(A6), .A5(A5), .A4(A4), .A3(A3), .A2(A2), .A1(A1),
    .A0(A0), .B7(B7), .B6(B6), .B5(B5), .B4(B4), .B3(B3), .B2(B2), .B1(B1), .B0(B0), .S7(S7), .S6(S6),
    .S5(S5), .S4(S4), .S3(S3), .S2(S2), .S1(S1), .S0(S0));
endmodule
